// Logisim project control-logic.circ as structural Verilog: 1 circuit, main circuit control_logic
module control_logic (
  input  [31:0] Instruction,
  input  BrEq,
  input  BrLt,
  output PCSel,
  output RegWEn,
  output [2:0] ImmSel,
  output BrUn,
  output ASel,
  output BSel,
  output [3:0] ALUSel,
  output MemWEn,
  output [1:0] WBSel
);

  wire funct3_g_1, funct3_is_0, funct3_is_1, is_add, is_addi, is_and, is_andi, is_auipc, is_beq, is_bge,
       is_bgeu, is_blt, is_bltu, is_bne, is_Itype, is_jal, is_jalr, is_lb, is_lh, is_lui, is_lw, is_mul,
       is_mulh, is_mulhu, is_or, is_ori, is_RIJBUtype, is_sb, is_sh, is_sll, is_slli, is_slt, is_slti,
       is_sra, is_srai, is_srl, is_srli, is_Stype, is_sub, is_sw, is_xor, is_xori;
  wire [5:0] priority_encoder_1_out;
  wire [15:14] rom_1_data;

  Comparator #(.width(3)) comparator_1 (
    .a(Instruction[6:4]), .b(3'b010), .gt(is_RIJBUtype), .eq(is_Stype), .lt(is_Itype));
  Priority_Encoder #(.select_enc(6)) priority_encoder_1 (
    .in0(is_add), .in1(is_mul), .in2(is_sub), .in3(is_sll), .in4(is_mulh), .in5(is_mulhu), .in6(is_slt),
    .in7(is_xor), .in8(is_srl), .in9(is_sra), .in10(is_or), .in11(is_and), .in12(is_lb), .in13(is_lh),
    .in14(is_lw), .in15(is_addi), .in16(is_slli), .in17(is_slti), .in18(is_xori), .in19(is_srli),
    .in20(is_srai), .in21(is_ori), .in22(is_andi), .in23(is_sb), .in24(is_sh), .in25(is_sw), .in26(is_beq),
    .in27(is_bne), .in28(is_blt), .in29(is_bge), .in30(is_bltu), .in31(is_bgeu), .in32(is_auipc),
    .in33(is_lui), .in34(is_jal), .in35(is_jalr), .out(priority_encoder_1_out));  // open: in36, in37, in38, in39, in40, in41, in42, in43, in44, in45, in46, in47, in48, in49, in50, in51, in52, in53, in54, in55, in56, in57, in58, in59, in60, in61, in62, in63, gs, en_out, en_in
  ROM #(.addrWidth(6), .dataWidth(16)) rom_1 (
    .addr(priority_encoder_1_out),
    .data({rom_1_data, WBSel, MemWEn, ALUSel, BSel, ASel, BrUn, ImmSel, RegWEn}));
  Comparator #(.width(3)) comparator_2 (
    .a(Instruction[14:12]), .b(3'b001), .gt(funct3_is_0), .eq(funct3_is_1), .lt(funct3_g_1));

  // Other names for the same wires on the sheet: opcode03[3:0] = Instruction[3:0]; opcode46[2:0] = Instruction[6:4];
  //   rd_imm[4:0] = Instruction[11:7]; funct3[2:0] = Instruction[14:12]; rs_imm[9:0] = Instruction[24:15];
  //   funct7[6:0] = Instruction[31:25]

  // Notes on the sheet:
  //   INPUTS to your circuit
  //   DON'T CHANGE THE LOCATIONS OF THE INPUTS AND OUTPUTS!
  //   Connect ROM Input here ->
  //   OUTPUT from your circuit
  //   contents of rom_1 (hex, n*v repeats v):
  //   102b 142b 162b 10ab 14ab 15ab 112b 122b 12ab 16ab 132b 13ab 61 61 61 1061 10e1 1161 1261 12e1 16e1
  //   1361 13e1 862 862 862 4*44 54 44 1047 17e7 2049 2061
  //   ROM FOR CONTROL LOGIC
  //   This is only if you choose to do the ROM option
  //   CONNECT
  //   WIRE
  //   TO
  //   USE
  //   ROM
  //   Reminder: If using ROM, use combinational logic for PCSel
endmodule
